// Logisim project Mips2v1.circ as structural Verilog: 51 circuits, main circuit MIPS
// MEM
module MIPS (
);

  wire clock_1_out, ex_mem_1_we, mem_wb_1_we, mipsprogramrom_1_p5;
  wire [1:0] ex_mem_1_dmem_2, ex_mem_1_pcsel_2, execute_1_dmem_2, execute_1_pcsel, id_ex_1_p27, id_ex_1_p28,
       id_ex_1_p29, instructiondecode_1_csel, instructiondecode_1_dmem, instructiondecode_1_sasel;
  wire [2:0] ex_mem_1__1bitcontrols_2, execute_1__1bitcontrols_2, id_ex_1_p25,
       instructiondecode_1__1bitcontrol, mem_wb_1__1bitcontrols_2, memory_1__1bitcontrols_2;
  wire [3:0] id_ex_1_p26, instructiondecode_1_alufunc;
  wire [4:0] ex_mem_1_rw_2, execute_1_r2_2, execute_1_rw_2, id_ex_1_p20, id_ex_1_p21, id_ex_1_p22,
       id_ex_1_p30, instructiondecode_1_branch_data, instructiondecode_1_rw, instructiondecode_1_shamt,
       mem_wb_1_rw_2, memory_1_rw_2, registerfile_1_p1, registerfile_1_p2, registerfile_1_p3;
  wire [5:0] ex_mem_1_opcode_2, execute_1_opcode_2, id_ex_1_p23, id_ex_1_p24, instructiondecode_1_func,
       instructiondecode_1_opcode;
  wire [25:0] instructiondecode_1_jump_target, instructiondecode_1_target;
  wire [31:0] ex_mem_1_b_2, ex_mem_1_d_2, ex_mem_1_pcabs_2, ex_mem_1_pcreg_2, ex_mem_1_pcrel_2, execute_1_b,
       execute_1_d, execute_1_pcabs, execute_1_pcreg, execute_1_pcrel, id_ex_1_p18, id_ex_1_p19, id_ex_1_p31,
       id_ex_1_p32, if_id_1_instr_2, if_id_1_pc_4_2, instructiondecode_1_imm, instructiondecode_1_pc_4_2,
       instructionfetch_1_pc, instructionfetch_1_pc_4, mem_wb_1_d_2, memory_1_d_2, memory_1_mem,
       mipsprogramrom_1_p2, mipsprogramrom_1_p3, registerfile_1_p4, registerfile_1_p5, registerfile_1_p6;

  Clock clock_1 (.out(clock_1_out));
  InstructionFetch instructionfetch_1 (
    .clock(clock_1_out), .pcsel(ex_mem_1_pcsel_2), .PC(instructionfetch_1_pc),
    .PC_4(instructionfetch_1_pc_4), .pcreg(ex_mem_1_pcreg_2), .pcrel(ex_mem_1_pcrel_2),
    .pcabs(ex_mem_1_pcabs_2));
  IF_ID if_id_1 (
    .clock(clock_1_out), .instr(mipsprogramrom_1_p2), .PC_4(instructionfetch_1_pc_4),
    .instr_2(if_id_1_instr_2), .PC_4_2(if_id_1_pc_4_2));
  // MIPSProgramROM mipsprogramrom_1: pin names not known; wires that end beside it: instructionfetch_1_pc, mipsprogramrom_1_p2, mipsprogramrom_1_p3, clock_1_out, mipsprogramrom_1_p5
  // RegisterFile registerfile_1: pin names not known; wires that end beside it: registerfile_1_p1, registerfile_1_p2, registerfile_1_p3, registerfile_1_p4, registerfile_1_p5, registerfile_1_p6
  InstructionDecode instructiondecode_1 (
    .instr(if_id_1_instr_2), .imm(instructiondecode_1_imm), .target(instructiondecode_1_target),
    .Opcode(instructiondecode_1_opcode), .R1(registerfile_1_p2), .shamt(instructiondecode_1_shamt),
    .func(instructiondecode_1_func), ._1bitControl(instructiondecode_1__1bitcontrol), .R2(registerfile_1_p3),
    .Csel(instructiondecode_1_csel), .SAsel(instructiondecode_1_sasel), .Rw(instructiondecode_1_rw),
    .ALUfunc(instructiondecode_1_alufunc), .PC_4(if_id_1_pc_4_2), .PC_4_2(instructiondecode_1_pc_4_2),
    .Dmem(instructiondecode_1_dmem), .jump_target(instructiondecode_1_jump_target),
    .branch_data(instructiondecode_1_branch_data));
  // ID_Ex id_ex_1: pin names not known; wires that end beside it: registerfile_1_p4, registerfile_1_p5, registerfile_1_p2, registerfile_1_p3, instructiondecode_1_rw, instructiondecode_1_opcode, instructiondecode_1_func, instructiondecode_1__1bitcontrol, instructiondecode_1_alufunc, instructiondecode_1_csel, instructiondecode_1_sasel, instructiondecode_1_dmem, instructiondecode_1_shamt, instructiondecode_1_imm, instructiondecode_1_target, instructiondecode_1_pc_4_2, clock_1_out, id_ex_1_p18, id_ex_1_p19, id_ex_1_p20, id_ex_1_p21, id_ex_1_p22, id_ex_1_p23, id_ex_1_p24, id_ex_1_p25, id_ex_1_p26, id_ex_1_p27, id_ex_1_p28, id_ex_1_p29, id_ex_1_p30, id_ex_1_p31, id_ex_1_p32
  BranchCalculate branchcalculate_1 (
    .branch_data(instructiondecode_1_branch_data), .A(registerfile_1_p4), .B(registerfile_1_p5),
    .PC(instructiondecode_1_pc_4_2), .jump(instructiondecode_1_jump_target));  // open: ifBranch, PCbranch
  Execute execute_1 (
    .A0(id_ex_1_p18), .B0(id_ex_1_p19), .Imm(id_ex_1_p31), .PC_4(id_ex_1_p32), .D(execute_1_d),
    .pcsel(execute_1_pcsel), .pcreg(execute_1_pcreg), .pcabs(execute_1_pcabs), .pcrel(execute_1_pcrel),
    .shamt(id_ex_1_p30), .func(id_ex_1_p24), .R1(id_ex_1_p20), .B(execute_1_b), .R2(id_ex_1_p21),
    .RW(id_ex_1_p22), .Rw_2(execute_1_rw_2), ._1bitControls(id_ex_1_p25), .SAsel(id_ex_1_p28),
    .Csel(id_ex_1_p27), ._1bitControls_2(execute_1__1bitcontrols_2), .R2_2(execute_1_r2_2),
    .ALUfunc(id_ex_1_p26), .M_W_WE(mem_wb_1_we), .E_M_WE(ex_mem_1_we), .EX_MEM_rW(ex_mem_1_rw_2),
    .WB_MEM_rW(mem_wb_1_rw_2), .E_M_D(ex_mem_1_d_2), .M_W_D(mem_wb_1_d_2), .Opcode(id_ex_1_p23),
    .Dmem(id_ex_1_p29), .Dmem_2(execute_1_dmem_2), .Opcode_2(execute_1_opcode_2));
  EX_MEM ex_mem_1 (
    .clock(clock_1_out), .D(execute_1_d), .pcreg(execute_1_pcreg), .pcrel(execute_1_pcrel),
    .pcabs(execute_1_pcabs), .pcsel(execute_1_pcsel), .D_2(ex_mem_1_d_2), .pcreg_2(ex_mem_1_pcreg_2),
    .pcrel_2(ex_mem_1_pcrel_2), .pcabs_2(ex_mem_1_pcabs_2), .pcsel_2(ex_mem_1_pcsel_2), .R2(execute_1_r2_2),
    .RW(execute_1_rw_2), ._1bitcontrols(execute_1__1bitcontrols_2),
    ._1bitcontrols_2(ex_mem_1__1bitcontrols_2), .RW_2(ex_mem_1_rw_2), .WE(ex_mem_1_we), .B(execute_1_b),
    .B_2(ex_mem_1_b_2), .Opcode(execute_1_opcode_2), .Opcode_2(ex_mem_1_opcode_2), .Dmem(execute_1_dmem_2),
    .Dmem_2(ex_mem_1_dmem_2));  // open: R2_2
  Memory memory_1 (
    .D(ex_mem_1_d_2), .B(ex_mem_1_b_2), .Opcode(ex_mem_1_opcode_2), .Dmem(ex_mem_1_dmem_2),
    .D_2(memory_1_d_2), .MEM(memory_1_mem), .clock(clock_1_out), .Rw_2(memory_1_rw_2), .Rw(ex_mem_1_rw_2),
    ._1BitControls(ex_mem_1__1bitcontrols_2), ._1BitControls_2(memory_1__1bitcontrols_2));
  MEM_WB mem_wb_1 (
    .clock(clock_1_out), .D(memory_1_d_2), .WE(mem_wb_1_we), .D_2(mem_wb_1_d_2), .RW(memory_1_rw_2),
    .RW_2(mem_wb_1_rw_2), ._1bitControls(memory_1__1bitcontrols_2),
    ._1bitControls_2(mem_wb_1__1bitcontrols_2), .Mem(memory_1_mem), .Mem_2(registerfile_1_p6));
  WriteBack writeback_1 (
    .D(mem_wb_1_d_2), .w(mipsprogramrom_1_p3), .Rw_2(registerfile_1_p1), .WE(mipsprogramrom_1_p5),
    .Rw(mem_wb_1_rw_2), ._1bitControls(mem_wb_1__1bitcontrols_2), .Mem(registerfile_1_p6));

  // Notes on the sheet:
  //   ROM
  //   Program Register
endmodule

// IF
module InstructionFetch (
  input  clock,
  input  [1:0] pcsel,
  input  [31:0] pcreg,
  input  [31:0] pcabs,
  input  [31:0] pcrel,
  output [31:0] PC,
  output [31:0] PC_4
);

  wire [31:0] register_1_q;

  // Probe on PC
  PC pc_1 (.pcsel(pcsel), .pcreg(pcreg), .pcabs(pcabs), .pcrel(pcrel), .PC_4(register_1_q), .PC(PC));
  _4 u_4_1 (.in(PC), .out(PC_4));
  Register #(.width(32)) register_1 (.D(PC_4), .Q(register_1_q), .clk(clock));  // open: en, clr
endmodule

module IF_ID (
  input  clock,
  input  [31:0] instr,
  input  [31:0] PC_4,
  output [31:0] instr_2,
  output [31:0] PC_4_2
);

  Register #(.width(32)) u_instr (.D(instr), .Q(instr_2), .clk(clock));  // open: en, clr
  Register #(.width(32)) u_PC_4 (.D(PC_4), .Q(PC_4_2), .clk(clock));  // open: en, clr
endmodule

// ID
module InstructionDecode (
  input  [31:0] instr,
  input  [31:0] PC_4,
  output [4:0] branch_data,
  output [25:0] jump_target,
  output [4:0] R1,
  output [4:0] R2,
  output [4:0] Rw,
  output [5:0] Opcode,
  output [2:0] _1bitControl,
  output [1:0] Csel,
  output [1:0] Dmem,
  output [1:0] SAsel,
  output [3:0] ALUfunc,
  output [5:0] func,
  output [4:0] shamt,
  output [25:0] target,
  output [31:0] imm,
  output [31:0] PC_4_2
);

  wire Branch_Decode_iflink;
  wire [1:0] decoder_1_dmem, decoder_1_wrs;
  wire [1:1] not_1_out;
  wire [4:0] Branch_Decode_rs, Branch_Decode_rt, decoder_1_r1, decoder_1_r2, decoder_1_r3;

  Branch_Detection Branch_Decode (
    .Instruction(instr), .ifReg(branch_data[3]), .ifLink(Branch_Decode_iflink),
    .BranchCond(branch_data[2:0]), .jump_target(jump_target), .rs(Branch_Decode_rs), .rt(Branch_Decode_rt),
    .ifBranchInstr(branch_data[4]));
  Decoder decoder_1 (
    .Opcode(Opcode), .Imm(imm), .Shamt(shamt), .R3(decoder_1_r3), .R2(decoder_1_r2), .R1(decoder_1_r1),
    .func(func), .Target(target), .Instruction(instr), ._1bitControl(_1bitControl), .SAsel(SAsel),
    .Wrs(decoder_1_wrs), .Csel(Csel), .ALUfunc(ALUfunc), .Dmem(decoder_1_dmem));
  Multiplexer #(.width(5), .enable("false")) multiplexer_1 (
    .in0(decoder_1_r1), .in1(Branch_Decode_rs), .out(R1), .sel(branch_data[4]));
  Multiplexer #(.width(5), .enable("false")) multiplexer_2 (
    .in0(decoder_1_r2), .in1(Branch_Decode_rt), .out(R2), .sel(branch_data[4]));
  not not_1 (not_1_out[1], branch_data[4]);
  assign Dmem = {2{not_1_out[1]}} & decoder_1_dmem;  // AND_Gate and_1, 2 bits wide
  Multiplexer #(.select(2), .width(5), .enable("false")) multiplexer_3 (
    .in0(R2), .in1(decoder_1_r3), .in2({5{1'b1}}), .in3({5{1'b1}}), .out(Rw), .sel(decoder_1_wrs));

  assign PC_4_2 = PC_4;
endmodule

// ID/EX
module ID_Ex (
  input  clock,
  input  [31:0] A,
  input  [31:0] B,
  input  [4:0] R1,
  input  [4:0] R2,
  input  [4:0] RW,
  input  [5:0] Opcode,
  input  [5:0] func,
  input  [2:0] _1bitControls,
  input  [3:0] ALUfunc,
  input  [1:0] Csel,
  input  [1:0] SAsel,
  input  [1:0] Dmem,
  input  [4:0] shamt,
  input  [31:0] imm,
  input  [25:0] target,
  input  [31:0] PC_4,
  output [31:0] A_2,
  output [31:0] B_2,
  output [4:0] r1_2,
  output [4:0] r2_2,
  output [4:0] rw_2,
  output [5:0] Opcode_2,
  output [5:0] func_2,
  output [2:0] _1bitBontrols,
  output [3:0] ALUfunc_2,
  output [1:0] Csel_2,
  output [1:0] SAsel_2,
  output [1:0] Dmem_2,
  output [4:0] shamt_2,
  output [31:0] imm_2,
  output [25:0] target_2,
  output [31:0] PC_4_2
);

  Register #(.width(32), .trigger("falling")) u_A (.D(A), .Q(A_2), .clk(clock));  // open: en, clr
  Register #(.width(32), .trigger("falling")) u_B (.D(B), .Q(B_2), .clk(clock));  // open: en, clr
  Register #(.width(5), .trigger("falling")) u_R1 (.D(R1), .Q(r1_2), .clk(clock));  // open: en, clr
  Register #(.width(5), .trigger("falling")) u_R2 (.D(R2), .Q(r2_2), .clk(clock));  // open: en, clr
  Register #(.width(5), .trigger("falling")) u_Rw (.D(RW), .Q(rw_2), .clk(clock));  // open: en, clr
  Register #(.width(6), .trigger("falling")) u_Opcode (.D(Opcode), .Q(Opcode_2), .clk(clock));  // open: en, clr
  Register #(.width(6), .trigger("falling")) u_func (.D(func), .Q(func_2), .clk(clock));  // open: en, clr
  Register #(.width(3), .trigger("falling")) u__1bitControls (
    .D(_1bitControls), .Q(_1bitBontrols), .clk(clock));  // open: en, clr
  Register #(.width(4), .trigger("falling")) u_ALUfunc (.D(ALUfunc), .Q(ALUfunc_2), .clk(clock));  // open: en, clr
  Register #(.width(2), .trigger("falling")) register_1 (.D(Csel), .Q(Csel_2), .clk(clock));  // open: en, clr
  Register #(.width(2), .trigger("falling")) register_2 (.D(SAsel), .Q(SAsel_2), .clk(clock));  // open: en, clr
  Register #(.width(2), .trigger("falling")) register_3 (.D(Dmem), .Q(Dmem_2), .clk(clock));  // open: en, clr
  Register #(.width(5), .trigger("falling")) u_Shamt (.D(shamt), .Q(shamt_2), .clk(clock));  // open: en, clr
  Register #(.width(32), .trigger("falling")) u_imm (.D(imm), .Q(imm_2), .clk(clock));  // open: en, clr
  Register #(.width(26), .trigger("falling")) u_target (.D(target), .Q(target_2), .clk(clock));  // open: en, clr
  Register #(.width(32), .trigger("falling")) u_PC_4 (.D(PC_4), .Q(PC_4_2), .clk(clock));  // open: en, clr
endmodule

// EX
module Execute (
  input  [31:0] A0,
  input  [31:0] B0,
  input  [3:0] ALUfunc,
  input  [5:0] func,
  input  [4:0] shamt,
  input  [1:0] SAsel,
  input  [4:0] R2,
  input  [4:0] RW,
  input  [2:0] _1bitControls,
  input  [1:0] Dmem,
  input  [1:0] Csel,
  input  [5:0] Opcode,
  input  [31:0] Imm,
  input  [31:0] PC_4,
  input  M_W_WE,
  input  E_M_WE,
  input  [4:0] EX_MEM_rW,
  input  [4:0] WB_MEM_rW,
  input  [4:0] R1,
  input  [31:0] M_W_D,
  input  [31:0] E_M_D,
  output [31:0] D,
  output [31:0] B,
  output [4:0] R2_2,
  output [4:0] Rw_2,
  output [2:0] _1bitControls_2,
  output [1:0] Dmem_2,
  output [5:0] Opcode_2,
  output [1:0] pcsel,
  output [31:0] pcreg,
  output [31:0] pcabs,
  output [31:0] pcrel
);

  wire comparator_1_lt, comparator_2_lt;
  wire [1:0] detecthazard_1_forwarda, detecthazard_1_forwardb;
  wire [4:0] mips_alu_1_p4;
  wire [31:0] B2, bit_extender_1_out, bit_extender_2_out, mips_alu_1_p5, multiplexer_1_out;

  Multiplexer #(.select(2), .width(32), .enable("false")) multiplexer_1 (
    .in0(pcreg), .in1(pcreg), .in2(pcreg), .in3({32{1'b0}}), .out(multiplexer_1_out), .sel(Csel));
  Multiplexer #(.width(32), .enable("false")) multiplexer_2 (.in0(B), .in1(Imm), .out(B2), .sel(_1bitControls[1]));
  DetectHazard detecthazard_1 (
    .M_W_WE(M_W_WE), .E_M_WE(E_M_WE), .E_M_rW(EX_MEM_rW), .M_W_rW(WB_MEM_rW), .D_E_Ra(R1), .D_E_Rb(R2),
    .ForwardA(detecthazard_1_forwarda), .ForwardB(detecthazard_1_forwardb));
  Multiplexer #(.select(2), .width(32), .enable("false")) multiplexer_3 (
    .in0(B0), .in1(M_W_D), .in2(E_M_D), .out(B), .sel(detecthazard_1_forwardb));  // open: in3
  // Mips_ALU mips_alu_1: pin names not known; wires that end beside it: multiplexer_1_out, B2, ALUfunc, mips_alu_1_p4, mips_alu_1_p5
  Multiplexer #(.select(2), .width(5), .enable("false")) multiplexer_4 (
    .in0(shamt), .in1(pcreg[4:0]), .in2(5'b10000), .out(mips_alu_1_p4), .sel(SAsel));  // open: in3
  PCcalc pccalc_1 (.Op(Opcode), .imm(Imm), .PC_4(PC_4), .pcsel(pcsel), .pcabs(pcabs), .pcrel(pcrel));
  Multiplexer #(.select(2), .width(32), .enable("false")) multiplexer_5 (
    .in0(A0), .in1(M_W_D), .in2(E_M_D), .out(pcreg), .sel(detecthazard_1_forwarda));  // open: in3
  Comparator #(.width(32)) comparator_1 (.a(pcreg), .b(B2), .lt(comparator_1_lt));  // open: gt, eq
  Comparator #(.width(32), .mode("unsigned")) comparator_2 (.a(pcreg), .b(B2), .lt(comparator_2_lt));  // open: gt, eq
  WE_2 we_2_1 (.func(func), .WE(_1bitControls[0]), .Opcode(Opcode), .D(mips_alu_1_p5), .WE_2(_1bitControls_2[0]));
  assign bit_extender_1_out = {{31{1'b0}}, comparator_1_lt};  // Bit_Extender bit_extender_1
  assign bit_extender_2_out = {{31{1'b0}}, comparator_2_lt};  // Bit_Extender bit_extender_2
  Multiplexer #(.select(2), .width(32), .enable("false")) multiplexer_6 (
    .in0(mips_alu_1_p5), .in1(bit_extender_1_out), .in2(bit_extender_2_out), .in3(pcreg), .out(D), .sel(Csel));

  assign _1bitControls_2[2:1] = _1bitControls[2:1];
  assign Dmem_2 = Dmem;
  assign Opcode_2 = Opcode;
  assign R2_2 = R2;
  assign Rw_2 = RW;

  // Other names for the same wires on the sheet: WE = _1bitControls[0]; ALUs = _1bitControls[1]; A[31:0] = pcreg

  // Notes on the sheet:
  //   C
endmodule

module EX_MEM (
  input  clock,
  input  [31:0] D,
  input  [31:0] B,
  input  [4:0] R2,
  input  [4:0] RW,
  input  [2:0] _1bitcontrols,
  input  [5:0] Opcode,
  input  [1:0] Dmem,
  input  [1:0] pcsel,
  input  [31:0] pcreg,
  input  [31:0] pcrel,
  input  [31:0] pcabs,
  output [31:0] D_2,
  output [31:0] B_2,
  output [4:0] R2_2,
  output [4:0] RW_2,
  output [2:0] _1bitcontrols_2,
  output WE,
  output [5:0] Opcode_2,
  output [1:0] Dmem_2,
  output [1:0] pcsel_2,
  output [31:0] pcreg_2,
  output [31:0] pcrel_2,
  output [31:0] pcabs_2
);

  Register #(.width(32)) u_D (.D(D), .Q(D_2), .clk(clock));  // open: en, clr
  Register #(.width(32)) u_B (.D(B), .Q(B_2), .clk(clock));  // open: en, clr
  Register #(.width(5)) u_R2 (.D(R2), .Q(R2_2), .clk(clock));  // open: en, clr
  Register #(.width(5)) R3 (.D(RW), .Q(RW_2), .clk(clock));  // open: en, clr
  Register #(.width(3)) u__1bitcontrols (.D(_1bitcontrols), .Q(_1bitcontrols_2), .clk(clock));  // open: en, clr
  Register #(.width(6), .trigger("falling")) u_Opcode (.D(Opcode), .Q(Opcode_2), .clk(clock));  // open: en, clr
  Register #(.width(2), .trigger("falling")) register_1 (.D(Dmem), .Q(Dmem_2), .clk(clock));  // open: en, clr
  Register #(.width(2)) u_pcsel (.D(pcsel), .Q(pcsel_2), .clk(clock));  // open: en, clr
  Register #(.width(32)) u_pcreg (.D(pcreg), .Q(pcreg_2), .clk(clock));  // open: en, clr
  Register #(.width(32)) u_pcrel (.D(pcrel), .Q(pcrel_2), .clk(clock));  // open: en, clr
  Register #(.width(32)) u_pcabs (.D(pcabs), .Q(pcabs_2), .clk(clock));  // open: en, clr

  assign WE = _1bitcontrols_2[0];

  // Notes on the sheet:
  //   _1bitcontrols_2: pull=up
endmodule

module MEM_WB (
  input  clock,
  input  [31:0] D,
  input  [31:0] Mem,
  input  [4:0] RW,
  input  [2:0] _1bitControls,
  output [31:0] D_2,
  output [31:0] Mem_2,
  output [4:0] RW_2,
  output WE,
  output [2:0] _1bitControls_2
);

  Register #(.width(32)) u_D (.D(D), .Q(D_2), .clk(clock));  // open: en, clr
  Register #(.width(32)) u_Mem (.D(Mem), .Q(Mem_2), .clk(clock));  // open: en, clr
  Register #(.width(5)) u_RW (.D(RW), .Q(RW_2), .clk(clock));  // open: en, clr
  Register #(.width(1)) u_WE (.D(_1bitControls[0]), .Q(WE), .clk(clock));  // open: en, clr
  Register #(.width(3)) u__1bitControls (.D(_1bitControls), .Q(_1bitControls_2), .clk(clock));  // open: en, clr
endmodule

// WB
module WriteBack (
  input  [31:0] D,
  input  [31:0] Mem,
  input  [2:0] _1bitControls,
  input  [4:0] Rw,
  output [31:0] w,
  output WE,
  output [4:0] Rw_2
);

  Multiplexer #(.width(32), .enable("false")) multiplexer_1 (.in0(D), .in1(Mem), .out(w), .sel(_1bitControls[2]));

  assign Rw_2 = Rw;
  assign WE = _1bitControls[0];
endmodule

module PC (
  input  [1:0] pcsel,
  input  [31:0] pcreg,
  input  [31:0] pcabs,
  input  [31:0] pcrel,
  input  [31:0] PC_4,
  output [31:0] PC
);

  Multiplexer #(.select(2), .width(32), .enable("false")) multiplexer_1 (
    .in0(PC_4), .in1(pcreg), .in2(pcabs), .in3(pcrel), .out(PC), .sel(pcsel));
  // Probe on PC
endmodule

module _4 (
  input  [31:0] in,
  output [31:0] out
);

  // Incrementer incrementer_1: pin names not known; wires that end beside it: in[31:2], out[31:2]

  assign out[1:0] = in[1:0];
endmodule

module Decoder (
  input  [31:0] Instruction,
  output [2:0] _1bitControl,
  output [1:0] Dmem,
  output [1:0] Wrs,
  output [1:0] Csel,
  output [1:0] SAsel,
  output [3:0] ALUfunc,
  output [5:0] Opcode,
  output [31:0] Imm,
  output [4:0] Shamt,
  output [4:0] R3,
  output [4:0] R2,
  output [4:0] R1,
  output [5:0] func,
  output [25:0] Target
);

  wire controlsign_1_extsel;

  ControlSign controlsign_1 (
    .func(Instruction[5:0]), .Opcode(Instruction[31:26]), .WE(_1bitControl[0]), .WRs(Wrs),
    .ALUs(_1bitControl[1]), .WBs(_1bitControl[2]), .Csel(Csel), .Extsel(controlsign_1_extsel), .SAsel(SAsel),
    .Dmem(Dmem));
  extend extend_1 (.Extsel(controlsign_1_extsel), .Imm(Instruction[15:0]), .imm_2(Imm));
  ALUop aluop_1 (.Opcode(Instruction[31:26]), .func(Instruction[5:0]), .ALUop(ALUfunc));

  assign func = Instruction[5:0];
  assign Opcode = Instruction[31:26];
  assign R1 = Instruction[25:21];
  assign R2 = Instruction[20:16];
  assign R3 = Instruction[15:11];
  assign Shamt = Instruction[10:6];
  assign Target = Instruction[25:0];

  // Notes on the sheet:
  //   extend
  //   ALUop
endmodule

// WE2
module WE_2 (
  input  [5:0] func,
  input  WE,
  input  [5:0] Opcode,
  input  [31:0] D,
  output WE_2
);

  wire and_1_out, and_2_out, and_3_out, isatype_1_isatype, not_1_out, not_2_out, not_3_out, not_4_out;

  not not_1 (not_1_out, func[5]);
  not not_2 (not_2_out, func[4]);
  not not_3 (not_3_out, func[2]);
  IsAtype isatype_1 (.Opcode(Opcode), .IsAtype(isatype_1_isatype));
  and and_1 (and_1_out, not_1_out, not_2_out, func[3], not_3_out, func[1], isatype_1_isatype);
  not not_4 (not_4_out, and_1_out);
  and and_2 (and_2_out, not_4_out, WE);
  or or_1 (WE_2, and_2_out, and_3_out);
  and and_3 (and_3_out, and_1_out, D[0]);
endmodule

// Hazard
module DetectHazard (
  input  M_W_WE,
  input  E_M_WE,
  input  [4:0] E_M_rW,
  input  [4:0] M_W_rW,
  input  [4:0] D_E_Ra,
  input  [4:0] D_E_Rb,
  output [1:0] ForwardA,
  output [1:0] ForwardB
);

  wire b_out_3, d_out_3, e_out_3, f_out_3, g_out_3, h_out_3;

  equals d (.a(E_M_rW), .b({5{1'b0}}), .out_3(d_out_3));
  equals b (.a({5{1'b0}}), .b(M_W_rW), .out_3(b_out_3));
  equals f (.a(E_M_rW), .b(D_E_Ra), .out_3(f_out_3));
  equals e (.a(M_W_rW), .b(D_E_Ra), .out_3(e_out_3));
  equals g (.a(M_W_rW), .b(D_E_Rb), .out_3(g_out_3));
  equals h (.a(E_M_rW), .b(D_E_Rb), .out_3(h_out_3));
  forwardhelper forwardhelper_1 (
    .a(M_W_WE), .b(b_out_3), .c(E_M_WE), .d(d_out_3), .e(e_out_3), .f(f_out_3), .g(g_out_3), .h(h_out_3),
    .fa2(ForwardA[0]), .fa1(ForwardA[1]), .fb2(ForwardB[0]), .fb1(ForwardB[1]));
endmodule

// Control Signals
module ControlSign (
  input  [5:0] func,
  input  [5:0] Opcode,
  output WE,
  output [1:0] WRs,
  output ALUs,
  output WBs,
  output [1:0] Dmem,
  output [1:0] Csel,
  output Extsel,
  output [1:0] SAsel
);

  WEv2 WEv2 (
    .op0(Opcode[0]), .op1(Opcode[1]), .op2(Opcode[2]), .op3(Opcode[3]), .op4(Opcode[4]), .op5(Opcode[5]),
    .f0(func[0]), .f1(func[1]), .f2(func[2]), .f3(func[3]), .f4(func[4]), .f5(func[5]), .WE(WE));
  WRs wrs_1 (.func(func), .Opcode(Opcode), .WRs(WRs));
  ALUs alus_1 (.Opcode(Opcode), .o(ALUs));
  WBs wbs_1 (.Opcode(Opcode), .WBs(WBs));
  Dmem dmem_1 (.Opcode(Opcode), .Dmem(Dmem));
  Csel csel_1 (.func(func), .opcode(Opcode), .C_sel(Csel));
  Extsel extsel_1 (.Opcode(Opcode), .extsel(Extsel));
  SAsel sasel_1 (.Opcode(Opcode), .func(func), .Shamt_sel(SAsel));
endmodule

module extend (
  input  Extsel,
  input  [15:0] Imm,
  output [31:0] imm_2
);

  wire [31:0] bit_extender_1_out, bit_extender_2_out;

  assign bit_extender_1_out = {{16{1'b0}}, Imm};  // Bit_Extender bit_extender_1
  assign bit_extender_2_out = {{16{Imm[15]}}, Imm};  // Bit_Extender bit_extender_2
  Multiplexer #(.width(32), .enable("false")) multiplexer_1 (
    .in0(bit_extender_1_out), .in1(bit_extender_2_out), .out(imm_2), .sel(Extsel));
endmodule

module PCcalc (
  input  [5:0] Op,
  input  [31:0] imm,
  input  [31:0] PC_4,
  output [1:0] pcsel,
  output [31:0] pcabs,
  output [31:0] pcrel
);

  pcsel_calc pcsel_calc_1 (.Op(Op), .out_2(pcsel));
  Adder #(.width(32)) adder_1 (.a(imm), .b(PC_4), .out(pcrel));  // open: cin, cout

  assign pcabs = imm;
endmodule

module pcsel_calc (
  input  [5:0] Op,
  output [1:0] out_2
);

  wire and_1_out, and_2_out, and_3_out, and_4_out, not_1_out, not_2_out, not_3_out, not_4_out, not_5_out,
       not_6_out, not_7_out, not_8_out, not_9_out, not_10_out, not_11_out, not_12_out, not_13_out,
       not_14_out, not_15_out, not_16_out, not_17_out;

  not not_1 (not_1_out, Op[5]);
  not not_2 (not_2_out, Op[4]);
  not not_3 (not_3_out, Op[3]);
  not not_4 (not_4_out, Op[1]);
  not not_5 (not_5_out, Op[5]);
  not not_6 (not_6_out, Op[4]);
  not not_7 (not_7_out, Op[2]);
  not not_8 (not_8_out, Op[1]);
  not not_9 (not_9_out, Op[0]);
  not not_10 (not_10_out, Op[5]);
  not not_11 (not_11_out, Op[4]);
  not not_12 (not_12_out, Op[3]);
  not not_13 (not_13_out, Op[2]);
  not not_14 (not_14_out, Op[5]);
  not not_15 (not_15_out, Op[4]);
  not not_16 (not_16_out, Op[3]);
  not not_17 (not_17_out, Op[1]);
  and and_1 (and_1_out, not_1_out, not_2_out, not_3_out, Op[2], not_4_out);
  and and_2 (and_2_out, not_5_out, not_6_out, Op[3], not_7_out, not_8_out, not_9_out);
  and and_3 (and_3_out, not_10_out, not_11_out, not_12_out, not_13_out, Op[1]);
  or or_1 (out_2[0], and_3_out, and_4_out);
  and and_4 (and_4_out, not_14_out, not_15_out, not_16_out, Op[2], not_17_out);
  or or_2 (out_2[1], and_1_out, and_2_out);
endmodule

// eq
module equals (
  input  [4:0] a,
  input  [4:0] b,
  output out_3
);

  wire [4:0] not_1_out, xor_1_out;

  assign xor_1_out = a ^ b;  // XOR_Gate xor_1, 5 bits wide
  assign not_1_out = ~xor_1_out;  // NOT_Gate not_1, 5 bits wide
  and and_1 (out_3, not_1_out[0], not_1_out[1], not_1_out[2], not_1_out[3], not_1_out[4]);
endmodule

module forwardhelper (
  input  a,
  input  b,
  input  c,
  input  d,
  input  e,
  input  f,
  input  g,
  input  h,
  output fa2,
  output fa1,
  output fb2,
  output fb1
);

  wire a___nb_out, and_1_out, and_2_out, c___nd_out, not_1_out, not_2_out, not_3_out, not_4_out;

  and a___nb (a___nb_out, a, not_1_out);
  not not_1 (not_1_out, b);
  and c___nd (c___nd_out, c, not_2_out);
  not not_2 (not_2_out, d);
  and and_1 (and_1_out, a___nb_out, e);
  and c_nd___f (fa1, c___nd_out, f);
  and and_2 (and_2_out, a___nb_out, g);
  and c_nd_h (fb1, c___nd_out, h);
  not not_3 (not_3_out, fa1);
  and and_3 (fa2, and_1_out, not_3_out);
  and and_4 (fb2, and_2_out, not_4_out);
  not not_4 (not_4_out, fb1);
endmodule

// IsA
module IsAtype (
  input  [5:0] Opcode,
  output IsAtype
);

  wire not_1_out, not_2_out, not_3_out, not_4_out, not_5_out, not_6_out;

  not not_1 (not_1_out, Opcode[5]);
  not not_2 (not_2_out, Opcode[4]);
  not not_3 (not_3_out, Opcode[3]);
  not not_4 (not_4_out, Opcode[2]);
  not not_5 (not_5_out, Opcode[1]);
  not not_6 (not_6_out, Opcode[0]);
  and and_1 (IsAtype, not_1_out, not_2_out, not_3_out, not_4_out, not_5_out, not_6_out);
endmodule

module ALUop_Atype (
  input  [5:0] func,
  output [3:0] ALUop
);

  wire and_1_out, and_2_out, and_3_out, and_4_out, and_5_out, and_6_out, and_7_out, and_8_out, not_1_out,
       not_2_out, not_3_out, not_4_out;

  not not_1 (not_1_out, func[5]);
  and and_1 (and_1_out, not_1_out, func[3]);
  and and_2 (and_2_out, func[5], func[2]);
  not not_2 (not_2_out, func[3]);
  and and_3 (and_3_out, not_2_out, func[1]);
  and and_4 (and_4_out, func[5], func[3]);
  and and_5 (and_5_out, func[3], func[0]);
  and and_6 (and_6_out, func[5], not_3_out);
  not not_3 (not_3_out, func[2]);
  and and_7 (and_7_out, func[5], func[0]);
  not not_4 (not_4_out, func[5]);
  and and_8 (and_8_out, not_4_out, func[0]);
  or or_1 (ALUop[3], and_1_out, and_2_out);
  or or_2 (ALUop[2], and_3_out, and_4_out);
  or or_3 (ALUop[1], and_5_out, and_6_out, and_7_out);
  or or_4 (ALUop[0], and_8_out, func[3]);
endmodule

module ALUop_notAtype (
  input  [5:0] Op,
  output [3:0] ALUop
);

  wire and_1_out, and_2_out, and_3_out, and_4_out, and_5_out, not_1_out, not_2_out, not_3_out, not_4_out,
       not_5_out, not_6_out;

  IsAtype isatype_1 (.Opcode(Op), .IsAtype(ALUop[0]));
  and and_1 (and_1_out, Op[2], not_1_out);
  not not_1 (not_1_out, Op[1]);
  and and_2 (and_2_out, Op[2], not_2_out);
  not not_2 (not_2_out, Op[0]);
  not not_3 (not_3_out, Op[2]);
  and and_3 (and_3_out, not_3_out, Op[1]);
  and and_4 (and_4_out, Op[1], not_4_out);
  not not_4 (not_4_out, Op[0]);
  not not_5 (not_5_out, Op[2]);
  not not_6 (not_6_out, Op[1]);
  and and_5 (and_5_out, not_6_out, Op[0]);
  or or_1 (ALUop[3], and_1_out, and_2_out);
  or or_2 (ALUop[2], and_3_out, and_4_out);
  or or_3 (ALUop[1], not_5_out, and_5_out);
endmodule

module ALUop (
  input  [5:0] Opcode,
  input  [5:0] func,
  output [3:0] ALUop
);

  wire isatype_1_isatype;
  wire [3:0] aluop_atype_1_aluop, aluop_notatype_1_aluop;

  ALUop_notAtype aluop_notatype_1 (.Op(Opcode), .ALUop(aluop_notatype_1_aluop));
  ALUop_Atype aluop_atype_1 (.func(func), .ALUop(aluop_atype_1_aluop));
  IsAtype isatype_1 (.Opcode(Opcode), .IsAtype(isatype_1_isatype));
  Multiplexer #(.width(4), .enable("false")) multiplexer_1 (
    .in0(aluop_notatype_1_aluop), .in1(aluop_atype_1_aluop), .out(ALUop), .sel(isatype_1_isatype));

  // Notes on the sheet:
  //   forItypes
  //   forAtypes
endmodule

module SAsel (
  input  [5:0] Opcode,
  input  [5:0] func,
  output [1:0] Shamt_sel
);

  wire not_1_out, not_2_out, not_3_out;

  not not_1 (not_1_out, Opcode[5]);
  not not_2 (not_2_out, Opcode[4]);
  and and_1 (Shamt_sel[1], not_1_out, not_2_out, Opcode[3], Opcode[2], Opcode[1], Opcode[0]);
  not not_3 (not_3_out, Shamt_sel[1]);
  and and_2 (Shamt_sel[0], not_3_out, func[2]);
endmodule

module Csel (
  input  [5:0] func,
  input  [5:0] opcode,
  output [1:0] C_sel
);

  wire and_1_out, and_2_out, and_3_out, and_4_out, and_5_out, and_6_out, and_7_out, and_8_out, and_9_out,
       and_10_out, isatype_1_isatype, not_1_out, not_2_out, not_3_out, not_4_out, not_5_out, not_6_out,
       not_7_out, not_8_out, not_9_out, not_10_out, or_1_out, or_2_out;

  IsAtype isatype_1 (.Opcode(opcode), .IsAtype(isatype_1_isatype));
  not not_1 (not_1_out, func[5]);
  not not_2 (not_2_out, func[5]);
  not not_3 (not_3_out, func[0]);
  not not_4 (not_4_out, opcode[5]);
  not not_5 (not_5_out, opcode[2]);
  not not_6 (not_6_out, opcode[5]);
  not not_7 (not_7_out, opcode[2]);
  not not_8 (not_8_out, opcode[0]);
  and and_1 (and_1_out, not_1_out, func[3]);
  and and_2 (and_2_out, func[3], func[0]);
  and and_3 (and_3_out, not_2_out, func[3]);
  and and_4 (and_4_out, func[3], not_3_out);
  and and_5 (and_5_out, not_4_out, not_5_out, opcode[1], opcode[0]);
  and and_6 (and_6_out, not_6_out, not_7_out, not_8_out);
  or or_1 (or_1_out, and_1_out, and_2_out);
  or or_2 (or_2_out, and_3_out, and_4_out);
  not not_9 (not_9_out, isatype_1_isatype);
  not not_10 (not_10_out, isatype_1_isatype);
  and and_7 (and_7_out, not_9_out, and_5_out);
  and and_8 (and_8_out, isatype_1_isatype, or_1_out);
  and and_9 (and_9_out, not_10_out, and_6_out);
  and and_10 (and_10_out, isatype_1_isatype, or_2_out);
  or or_3 (C_sel[1], and_7_out, and_8_out);
  or or_4 (C_sel[0], and_9_out, and_10_out);
endmodule

module WE (
  input  [5:0] Opcode,
  output WE
);

  wire and_1_out, and_2_out, and_3_out, and_4_out, not_1_out, not_2_out, not_3_out, not_4_out, not_5_out,
       not_6_out, not_7_out, not_8_out;

  not not_1 (not_1_out, Opcode[3]);
  not not_2 (not_2_out, Opcode[2]);
  not not_3 (not_3_out, Opcode[1]);
  not not_4 (not_4_out, Opcode[0]);
  not not_5 (not_5_out, Opcode[3]);
  not not_6 (not_6_out, Opcode[2]);
  and and_1 (and_1_out, not_1_out, not_2_out, not_3_out, not_4_out);
  and and_2 (and_2_out, not_5_out, not_6_out, Opcode[1], Opcode[0]);
  not not_7 (not_7_out, Opcode[5]);
  and and_3 (and_3_out, not_7_out, Opcode[3]);
  and and_4 (and_4_out, Opcode[5], not_8_out);
  not not_8 (not_8_out, Opcode[3]);
  or or_1 (WE, and_1_out, and_2_out, and_3_out, and_4_out);
endmodule

module ALUs (
  input  [5:0] Opcode,
  output o
);

  wire and_1_out, and_2_out, and_3_out, not_1_out, not_2_out, not_3_out, not_4_out;

  not not_1 (not_1_out, Opcode[4]);
  not not_2 (not_2_out, Opcode[2]);
  not not_3 (not_3_out, Opcode[4]);
  not not_4 (not_4_out, Opcode[4]);
  and and_1 (and_1_out, not_1_out, not_2_out, Opcode[1]);
  and and_2 (and_2_out, not_3_out, Opcode[3], Opcode[0]);
  and and_3 (and_3_out, not_4_out, Opcode[3], Opcode[2]);
  or or_1 (o, and_1_out, and_2_out, and_3_out, Opcode[5]);
endmodule

module WBs (
  input  [5:0] Opcode,
  output WBs
);


  assign WBs = Opcode[5];
endmodule

module Dmem (
  input  [5:0] Opcode,
  output [1:0] Dmem
);

  wire and_1_out, and_2_out, and_3_out, and_4_out, not_1_out, not_2_out, not_3_out, not_4_out, not_5_out,
       not_6_out, not_7_out, not_8_out, not_9_out, not_10_out, not_11_out, not_12_out, not_13_out;

  not not_1 (not_1_out, Opcode[4]);
  not not_2 (not_2_out, Opcode[2]);
  not not_3 (not_3_out, Opcode[1]);
  not not_4 (not_4_out, Opcode[0]);
  not not_5 (not_5_out, Opcode[4]);
  not not_6 (not_6_out, Opcode[2]);
  not not_7 (not_7_out, Opcode[4]);
  not not_8 (not_8_out, Opcode[3]);
  not not_9 (not_9_out, Opcode[1]);
  not not_10 (not_10_out, Opcode[0]);
  not not_11 (not_11_out, Opcode[4]);
  not not_12 (not_12_out, Opcode[3]);
  not not_13 (not_13_out, Opcode[2]);
  and and_1 (and_1_out, Opcode[5], not_1_out, Opcode[3], not_2_out, not_3_out, not_4_out);
  and and_2 (and_2_out, Opcode[5], not_5_out, Opcode[3], not_6_out, Opcode[1], Opcode[0]);
  and and_3 (and_3_out, Opcode[5], not_7_out, not_8_out, not_9_out, not_10_out);
  and and_4 (and_4_out, Opcode[5], not_11_out, not_12_out, not_13_out, Opcode[1], Opcode[0]);
  or or_1 (Dmem[1], and_1_out, and_2_out);
  or or_2 (Dmem[0], and_3_out, and_4_out);
endmodule

module Extsel (
  input  [5:0] Opcode,
  output extsel
);

  wire not_1_out, not_2_out;

  not not_1 (not_1_out, Opcode[3]);
  or or_1 (extsel, not_1_out, not_2_out);
  not not_2 (not_2_out, Opcode[2]);
endmodule

module WRs (
  input  [5:0] func,
  input  [5:0] Opcode,
  output [1:0] WRs
);

  wire and_1_out, and_2_out, and_3_out, and_4_out, and_5_out, and_6_out, and_7_out, and_8_out, and_9_out,
       and_10_out, isatype_1_isatype, not_1_out, not_2_out, not_3_out, not_4_out, not_5_out, not_6_out,
       not_7_out, not_8_out, not_9_out, or_1_out, or_2_out, or_3_out;

  IsAtype isatype_1 (.Opcode(Opcode), .IsAtype(isatype_1_isatype));
  not not_1 (not_1_out, func[1]);
  not not_2 (not_2_out, func[3]);
  and and_1 (and_1_out, func[3], not_1_out);
  and and_2 (and_2_out, isatype_1_isatype, not_2_out);
  or or_1 (or_1_out, func[1], and_2_out);
  not not_3 (not_3_out, isatype_1_isatype);
  not not_4 (not_4_out, Opcode[5]);
  not not_5 (not_5_out, Opcode[3]);
  not not_6 (not_6_out, Opcode[1]);
  not not_7 (not_7_out, Opcode[3]);
  and and_3 (and_3_out, not_3_out, not_4_out, not_5_out, Opcode[1]);
  and and_4 (and_4_out, isatype_1_isatype, Opcode[3], not_6_out);
  and and_5 (and_5_out, isatype_1_isatype, not_7_out);
  and and_6 (and_6_out, isatype_1_isatype, Opcode[1]);
  or or_2 (or_2_out, and_3_out, and_4_out);
  or or_3 (or_3_out, and_5_out, and_6_out);
  not not_8 (not_8_out, isatype_1_isatype);
  and and_7 (and_7_out, not_8_out, or_2_out);
  and and_8 (and_8_out, isatype_1_isatype, and_1_out);
  not not_9 (not_9_out, isatype_1_isatype);
  and and_9 (and_9_out, not_9_out, or_3_out);
  and and_10 (and_10_out, isatype_1_isatype, or_1_out);
  or or_4 (WRs[1], and_7_out, and_8_out);
  or or_5 (WRs[0], and_9_out, and_10_out);
endmodule

module ALUselect (
  input  a,
  input  b,
  input  c,
  input  d,
  input  e,
  input  f,
  output o
);

  wire and_1_out, and_2_out, and_3_out, not_1_out, not_2_out, not_3_out, not_4_out;

  not not_1 (not_1_out, b);
  not not_2 (not_2_out, d);
  not not_3 (not_3_out, b);
  not not_4 (not_4_out, b);
  and and_1 (and_1_out, not_1_out, not_2_out, e);
  and and_2 (and_2_out, not_3_out, c, f);
  and and_3 (and_3_out, not_4_out, c, d);
  or or_1 (o, and_1_out, and_2_out, and_3_out, a);
endmodule

// Helper
module RegisterForwardHelper (
  input  _1steq,
  input  _1steq0,
  input  _2ndeq,
  input  _2ndeq0,
  input  we,
  input  clc,
  output Clock
);

  wire and_1_out, and_2_out, and_3_out, and_4_out, and_5_out, and_6_out, and_7_out, not_1_out, not_2_out,
       not_3_out, not_4_out, not_5_out, not_6_out, not_7_out, not_8_out, not_9_out;

  not not_1 (not_1_out, _1steq);
  not not_2 (not_2_out, _2ndeq);
  not not_3 (not_3_out, we);
  not not_4 (not_4_out, _1steq);
  not not_5 (not_5_out, _2ndeq0);
  not not_6 (not_6_out, clc);
  not not_7 (not_7_out, _2ndeq);
  not not_8 (not_8_out, _1steq0);
  not not_9 (not_9_out, clc);
  and and_1 (and_1_out, not_1_out, not_2_out, clc);
  and and_2 (and_2_out, not_3_out, clc);
  and and_3 (and_3_out, not_4_out, _2ndeq0, clc);
  and and_4 (and_4_out, _2ndeq, not_5_out, we, not_6_out);
  and and_5 (and_5_out, _1steq0, not_7_out, clc);
  and and_6 (and_6_out, _1steq0, _2ndeq0, clc);
  and and_7 (and_7_out, _1steq, not_8_out, we, not_9_out);
  or or_1 (Clock, and_1_out, and_2_out, and_3_out, and_4_out, and_5_out, and_6_out, and_7_out);
endmodule

// MEM
module Memory (
  input  clock,
  input  [31:0] D,
  input  [31:0] B,
  input  [5:0] Opcode,
  input  [1:0] Dmem,
  input  [2:0] _1BitControls,
  input  [4:0] Rw,
  output [31:0] D_2,
  output [31:0] MEM,
  output [2:0] _1BitControls_2,
  output [4:0] Rw_2
);

  wire [1:0] srl2_1_remainder;
  wire [3:0] sel_1_out_3;
  wire [31:0] srl2_1_d_4;

  // Probe on D
  SRL2 srl2_1 (.D(D), .D_4(srl2_1_d_4), .Remainder(srl2_1_remainder));
  sel sel_1 (.Remainder(srl2_1_remainder), .Opcode(Opcode), .out_3(sel_1_out_3));
  // MIPS_RAM mips_ram_1: pin names not known; wires that end beside it: srl2_1_d_4[19:0], B, Dmem[1], sel_1_out_3, clock, Dmem[0], MEM

  assign _1BitControls_2 = _1BitControls;
  assign D_2 = D;
  assign Rw_2 = Rw;
endmodule

module SRL2 (
  input  [31:0] D,
  output [1:0] Remainder,
  output [31:0] D_4
);

  // Probe on D
  // Probe on D[1:0]
  // Probe on {2'b00, D[31:2]}

  assign D_4 = {2'b00, D[31:2]};
  assign Remainder = D[1:0];
endmodule

module sel (
  input  [1:0] Remainder,
  input  [5:0] Opcode,
  output [3:0] out_3
);

  wire and_1_out, and_2_out, and_3_out, and_4_out, issworlw_1_issworlw, not_1_out, not_2_out, not_3_out,
       not_4_out;

  isSWorLW issworlw_1 (.Opcode(Opcode), .isSWorLW(issworlw_1_issworlw));
  and and_1 (and_1_out, Remainder[1], Remainder[0]);
  not not_1 (not_1_out, Remainder[0]);
  not not_2 (not_2_out, Remainder[1]);
  not not_3 (not_3_out, Remainder[1]);
  not not_4 (not_4_out, Remainder[0]);
  or or_1 (out_3[3], issworlw_1_issworlw, and_1_out);
  and and_2 (and_2_out, Remainder[1], not_1_out);
  and and_3 (and_3_out, not_2_out, Remainder[0]);
  and and_4 (and_4_out, not_3_out, not_4_out);
  or or_2 (out_3[2], issworlw_1_issworlw, and_2_out);
  or or_3 (out_3[1], issworlw_1_issworlw, and_3_out);
  or or_4 (out_3[0], and_4_out, issworlw_1_issworlw);

  // Notes on the sheet:
  //   isSW/LW
endmodule

module isSWorLW (
  input  [5:0] Opcode,
  output isSWorLW
);


  assign isSWorLW = Opcode[0];
endmodule

module dm (
  input  rem5,
  input  rem4,
  input  rem3,
  input  rem2,
  input  rem1,
  input  rem0,
  output d1,
  output d0
);

  wire and_1_out, and_2_out, and_3_out, and_4_out, not_1_out, not_2_out, not_3_out, not_4_out, not_5_out,
       not_6_out, not_7_out, not_8_out, not_9_out, not_10_out, not_11_out, not_12_out, not_13_out;

  not not_1 (not_1_out, rem4);
  not not_2 (not_2_out, rem2);
  not not_3 (not_3_out, rem1);
  not not_4 (not_4_out, rem0);
  not not_5 (not_5_out, rem4);
  not not_6 (not_6_out, rem2);
  not not_7 (not_7_out, rem4);
  not not_8 (not_8_out, rem3);
  not not_9 (not_9_out, rem1);
  not not_10 (not_10_out, rem0);
  not not_11 (not_11_out, rem4);
  not not_12 (not_12_out, rem3);
  not not_13 (not_13_out, rem2);
  and and_1 (and_1_out, rem5, not_1_out, rem3, not_2_out, not_3_out, not_4_out);
  and and_2 (and_2_out, rem5, not_5_out, rem3, not_6_out, rem1, rem0);
  and and_3 (and_3_out, rem5, not_7_out, not_8_out, not_9_out, not_10_out);
  and and_4 (and_4_out, rem5, not_11_out, not_12_out, not_13_out, rem1, rem0);
  or or_1 (d1, and_1_out, and_2_out);
  or or_2 (d0, and_3_out, and_4_out);
endmodule

module Branch_Detection (
  input  [31:0] Instruction,
  output ifReg,
  output ifLink,
  output [2:0] BranchCond,
  output [25:0] jump_target,
  output [4:0] rs,
  output [4:0] rt,
  output ifBranchInstr
);

  Branch_Decode Signal_Decoder (
    .Op(Instruction[31:26]), .func(Instruction[5:0]), .rt(Instruction[20:16]), .ifReg(ifReg),
    .ifLink(ifLink), .branch_control(BranchCond), .ifBranch(ifBranchInstr));

  assign jump_target = Instruction[25:0];
  assign rs = Instruction[20:16];
  assign rt = Instruction[25:21];
endmodule

module Branch_Decode (
  input  [5:0] Op,
  input  [5:0] func,
  input  [4:0] rt,
  output ifReg,
  output ifLink,
  output [2:0] branch_control,
  output ifBranch
);

  ifReg u_ifReg (.op0(Op[0]), .op1(Op[1]), .op2(Op[2]), .op3(Op[3]), .op4(Op[4]), .op5(Op[5]), .ifReg(ifReg));
  ifBranch u_ifBranch (
    .Op0(Op[0]), .Op1(Op[1]), .Op2(Op[2]), .Op3(Op[3]), .Op4(Op[4]), .Op5(Op[5]), .f0(func[0]), .f1(func[1]),
    .f2(func[2]), .f3(func[3]), .f4(func[4]), .f5(func[5]), .ifBranch(ifBranch));
  ifLink u_ifLink (
    .op0(Op[0]), .op1(Op[1]), .op2(Op[2]), .op3(Op[3]), .op4(Op[4]), .op5(Op[5]), .f0(func[0]), .f1(func[1]),
    .f2(func[2]), .f3(func[3]), .f4(func[4]), .f5(func[5]), .ifLink(ifLink));
  branchControl u_branch_control (
    .op0(rt[0]), .op1(rt[1]), .op2(rt[2]), .op3(rt[3]), .op4(rt[4]), .op5(Op[0]), .rt0(Op[1]), .rt1(Op[2]),
    .rt2(Op[3]), .rt3(Op[4]), .rt4(Op[5]), .bc0(branch_control[0]), .bc1(branch_control[1]),
    .bc2(branch_control[2]));
endmodule

module ifBranch (
  input  Op0,
  input  Op1,
  input  Op2,
  input  Op3,
  input  Op4,
  input  Op5,
  input  f0,
  input  f1,
  input  f2,
  input  f3,
  input  f4,
  input  f5,
  output ifBranch
);

  wire and_1_out, not_1_out, not_2_out, not_3_out, not_4_out, not_5_out, not_6_out, not_7_out, or_1_out;

  not not_1 (not_1_out, f5);
  not not_2 (not_2_out, f4);
  not not_3 (not_3_out, f2);
  not not_4 (not_4_out, f1);
  and and_1 (and_1_out, not_1_out, not_2_out, f3, not_3_out, not_4_out);
  not not_5 (not_5_out, Op5);
  not not_6 (not_6_out, Op4);
  not not_7 (not_7_out, Op3);
  or or_1 (or_1_out, Op2, Op1, Op0, and_1_out);
  and and_2 (ifBranch, not_5_out, not_6_out, not_7_out, or_1_out);
endmodule

module ifReg (
  input  op0,
  input  op1,
  input  op2,
  input  op3,
  input  op4,
  input  op5,
  output ifReg
);

  wire not_1_out, not_2_out, not_3_out, not_4_out;

  not not_1 (not_1_out, op5);
  not not_2 (not_2_out, op4);
  not not_3 (not_3_out, op3);
  not not_4 (not_4_out, op2);
  nand nand_1 (ifReg, not_1_out, not_2_out, not_3_out, not_4_out, op1);
endmodule

module ifLink (
  input  op0,
  input  op1,
  input  op2,
  input  op3,
  input  op4,
  input  op5,
  input  f0,
  input  f1,
  input  f2,
  input  f3,
  input  f4,
  input  f5,
  output ifLink
);

  wire and_1_out, and_2_out, not_1_out, not_2_out, not_3_out, not_4_out, not_5_out, not_6_out, not_7_out,
       not_8_out, not_9_out, not_10_out, not_11_out, not_12_out, not_13_out, not_14_out;

  not not_1 (not_1_out, op5);
  not not_2 (not_2_out, op4);
  not not_3 (not_3_out, op3);
  not not_4 (not_4_out, op2);
  not not_5 (not_5_out, op1);
  not not_6 (not_6_out, op0);
  not not_7 (not_7_out, f5);
  not not_8 (not_8_out, f4);
  not not_9 (not_9_out, f2);
  not not_10 (not_10_out, f1);
  not not_11 (not_11_out, op5);
  not not_12 (not_12_out, op4);
  not not_13 (not_13_out, op3);
  not not_14 (not_14_out, op2);
  and and_1 (and_1_out, not_1_out, not_2_out, not_3_out, not_4_out, not_5_out, not_6_out, not_7_out, not_8_out, f3, not_9_out, not_10_out, f0);
  and and_2 (and_2_out, not_11_out, not_12_out, not_13_out, not_14_out, op1, op0);
  or or_1 (ifLink, and_1_out, and_2_out);
endmodule

module branchControl (
  input  op0,
  input  op1,
  input  op2,
  input  op3,
  input  op4,
  input  op5,
  input  rt0,
  input  rt1,
  input  rt2,
  input  rt3,
  input  rt4,
  output bc0,
  output bc1,
  output bc2
);

  wire and_1_out, and_2_out, and_3_out, and_4_out, nand_1_out, not_1_out, not_2_out, not_3_out, not_4_out,
       not_5_out, not_6_out, not_7_out, not_8_out, not_9_out, not_10_out, not_11_out, not_12_out, not_13_out,
       not_14_out, not_15_out, not_16_out, not_17_out, not_18_out;

  not not_1 (not_1_out, op5);
  not not_2 (not_2_out, op4);
  not not_3 (not_3_out, op3);
  not not_4 (not_4_out, op2);
  not not_5 (not_5_out, op1);
  not not_6 (not_6_out, rt4);
  not not_7 (not_7_out, rt3);
  not not_8 (not_8_out, rt2);
  not not_9 (not_9_out, rt1);
  not not_10 (not_10_out, op5);
  not not_11 (not_11_out, op4);
  not not_12 (not_12_out, op3);
  not not_13 (not_13_out, op2);
  not not_14 (not_14_out, op1);
  not not_15 (not_15_out, op5);
  not not_16 (not_16_out, op4);
  not not_17 (not_17_out, op3);
  not not_18 (not_18_out, op0);
  or or_1 (bc1, op1, nand_1_out);
  nand nand_1 (nand_1_out, op5, op4, op3, op2, op1, op0);
  and and_1 (and_1_out, not_10_out, not_11_out, not_12_out, not_13_out, not_14_out, op0);
  and and_2 (and_2_out, not_15_out, not_16_out, not_17_out, op2, op1);
  and and_3 (and_3_out, op2, not_18_out);
  and and_4 (and_4_out, not_1_out, not_2_out, not_3_out, not_4_out, not_5_out, op0, not_6_out, not_7_out, not_8_out, not_9_out, rt0);
  or or_2 (bc2, and_1_out, and_2_out);
  or or_3 (bc0, and_3_out, and_4_out);
endmodule

module WEv2 (
  input  op0,
  input  op1,
  input  op2,
  input  op3,
  input  op4,
  input  op5,
  input  f0,
  input  f1,
  input  f2,
  input  f3,
  input  f4,
  input  f5,
  output WE
);

  wire and_1_out, and_2_out, and_3_out, and_4_out, nand_1_out, nor_1_out, not_1_out, not_2_out, not_3_out,
       not_4_out, not_5_out, not_6_out, not_7_out, not_8_out, not_9_out, not_10_out, not_11_out, not_12_out,
       not_13_out;

  not not_1 (not_1_out, f5);
  not not_2 (not_2_out, f4);
  not not_3 (not_3_out, f2);
  not not_4 (not_4_out, f1);
  not not_5 (not_5_out, f0);
  nor nor_1 (nor_1_out, op0, op1, op2, op3, op4, op5);
  nand nand_1 (nand_1_out, not_1_out, not_2_out, f3, not_3_out, not_4_out, not_5_out);
  not not_6 (not_6_out, op5);
  not not_7 (not_7_out, op4);
  not not_8 (not_8_out, op4);
  not not_9 (not_9_out, op3);
  not not_10 (not_10_out, op5);
  not not_11 (not_11_out, op4);
  not not_12 (not_12_out, op3);
  not not_13 (not_13_out, op2);
  and and_1 (and_1_out, nor_1_out, nand_1_out);
  and and_2 (and_2_out, not_6_out, not_7_out, op3);
  and and_3 (and_3_out, op5, not_8_out, not_9_out);
  and and_4 (and_4_out, not_10_out, not_11_out, not_12_out, not_13_out, op1, op0);
  or or_1 (WE, and_1_out, and_2_out, and_3_out, and_4_out);
endmodule

// Branch
module BranchCalculate (
  input  [4:0] branch_data,
  input  [31:0] A,
  input  [31:0] B,
  input  [31:0] PC,
  input  [25:0] jump,
  output ifBranch,
  output [31:0] PCbranch
);

  Multiplexer #(.width(32), .enable("false")) multiplexer_1 (
    .in0({PC[31:28], jump, 2'b00}), .in1(A), .out(PCbranch), .sel(branch_data[3]));
  BranchConditions branch_condition (
    .ifBranch(branch_data[4]), .branch_control(branch_data[2:0]), .A(A), .B(B), .ifBranch_2(ifBranch));
endmodule

module BranchConditions (
  input  ifBranch,
  input  [2:0] branch_control,
  input  [31:0] A,
  input  [31:0] B,
  output ifBranch_2
);

  wire eq32_1_eq, eqz_1_eq0, ltz_1_ltz, multiplexer_1_out, nor_1_out, not_1_out, xor_1_out, xor_2_out,
       xor_3_out;

  EQ32 eq32_1 (.A(A), .B(B), .eq(eq32_1_eq));
  EQZ eqz_1 (.B(B), .eq0(eqz_1_eq0));
  LTZ ltz_1 (.A(B), .LTZ(ltz_1_ltz));
  not not_1 (not_1_out, branch_control[0]);
  nor nor_1 (nor_1_out, eqz_1_eq0, ltz_1_ltz);
  xor xor_1 (xor_1_out, not_1_out, eq32_1_eq);
  xor xor_2 (xor_2_out, not_1_out, nor_1_out);
  xor xor_3 (xor_3_out, not_1_out, ltz_1_ltz);
  Multiplexer #(.select(2), .enable("false")) multiplexer_1 (
    .in0(xor_3_out), .in1(xor_2_out), .in2(xor_1_out), .in3(1'b1), .out(multiplexer_1_out),
    .sel(branch_control[2:1]));
  and and_1 (ifBranch_2, ifBranch, multiplexer_1_out);
endmodule

// =
module EQ32 (
  input  [31:0] A,
  input  [31:0] B,
  output eq
);

  wire [31:0] xor_1_out;

  assign xor_1_out = A ^ B;  // XOR_Gate xor_1, 32 bits wide
  EQZ eqz_1 (.B(xor_1_out), .eq0(eq));
endmodule

// <0
module LTZ (
  input  [31:0] A,
  output LTZ
);


  assign LTZ = A[31];
endmodule

// =0
module EQZ (
  input  [31:0] B,
  output eq0
);

  nor nor_1 (eq0, B[0], B[1], B[2], B[3], B[4], B[5], B[6], B[7], B[8], B[9], B[10], B[11], B[12], B[13], B[14], B[15], B[17], B[18], B[19], B[20], B[21], B[22], B[23], B[24], B[25], B[26], B[27], B[28], B[29], B[30], B[31], B[16]);
endmodule
