// Logisim project Project2.circ as structural Verilog: 9 circuits, main circuit MIPS
module MIPS (
);

  wire Clock_out, Decode_we, Execute_we_2, Memory_we_2, not_1_out, or_1_out, registerfile_1_p3,
       registerfile_1_p9, S_U_q, undriven, WE_2_q, WE_q;
  wire [3:0] Decode_alu0, Hazard_mem_wb_a_hazard, Op_2_q;
  wire [4:0] Control_q, Decode_c0, Execute_rd_2, Memory_rd_2, ra_q, rb_q, rd_2_q, rd_q, registerfile_1_p4,
       Sa_q;
  wire [5:0] multiplexer_1_out;
  wire [31:0] A_q, add4_1_c, B_q, bit_extender_1_out, C_q, Execute_c, Execute_pc_2, I_q, Memory_c_2,
       mipsprogramrom_1_p2, multiplexer_2_out, Op_q, PC_2_q, PC_3_q, PC_4_q, PC_q, registerfile_1_p1,
       registerfile_1_p7, registerfile_1_p8;

  add4 add4_1 (.A(PC_q), .C(add4_1_c));
  Clock Clock (.out(Clock_out));
  Register #(.width(32)) PC (.D(add4_1_c), .Q(PC_q), .clk(Clock_out));  // open: en, clr
  // MIPSProgramROM mipsprogramrom_1: pin names not known; wires that end beside it: PC_q, mipsprogramrom_1_p2
  Register #(.width(32)) Op (.D(mipsprogramrom_1_p2), .Q(Op_q), .clk(Clock_out));  // open: en, clr
  Register #(.width(32)) PC_2 (.D(add4_1_c), .Q(PC_2_q), .clk(Clock_out));  // open: en, clr
  not not_1 (not_1_out, Clock_out);
  // RegisterFile registerfile_1: pin names not known; wires that end beside it: registerfile_1_p1, not_1_out, registerfile_1_p3, registerfile_1_p4, Op_q[25:21], Op_q[20:16], registerfile_1_p7, registerfile_1_p8, registerfile_1_p9
  or or_1 (or_1_out, Op_q[26], Op_q[27], Op_q[28], Op_q[29], Op_q[30], Op_q[31]);
  Multiplexer #(.width(6)) multiplexer_1 (
    .in0(Op_q[5:0]), .in1({6{1'b0}}), .out(multiplexer_1_out), .sel(or_1_out));  // open: en
  assign bit_extender_1_out = {{16{Op_q[15]}}, Op_q[15:0]};  // Bit_Extender bit_extender_1
  Decode Decode (
    .f5(multiplexer_1_out[5]), .f4(multiplexer_1_out[4]), .f3(multiplexer_1_out[3]),
    .f2(multiplexer_1_out[2]), .f1(multiplexer_1_out[1]), .f0(multiplexer_1_out[0]), .op5(Op_q[31]),
    .op4(Op_q[30]), .op3(Op_q[29]), .op2(Op_q[28]), .op1(Op_q[27]), .op0(Op_q[26]), .LUI(registerfile_1_p9),
    .c4(Decode_c0[4]), .c3(Decode_c0[3]), .c2(Decode_c0[2]), .c1(Decode_c0[1]), .c0(Decode_c0[0]),
    .alu3(Decode_alu0[3]), .alu2(Decode_alu0[2]), .alu1(Decode_alu0[1]), .alu0(Decode_alu0[0]), .WE(Decode_we));
  Multiplexer #(.width(32), .enable("false")) multiplexer_2 (
    .in0(bit_extender_1_out), .in1({Op_q[15:0], {16{1'b0}}}), .out(multiplexer_2_out), .sel(registerfile_1_p9));
  Register #(.width(32)) A (.D(registerfile_1_p7), .Q(A_q), .clk(Clock_out));  // open: en, clr
  Register #(.width(5)) ra (.D(Op_q[25:21]), .Q(ra_q), .clk(Clock_out));  // open: en, clr
  Register #(.width(32)) B (.D(registerfile_1_p8), .Q(B_q), .clk(Clock_out));  // open: en, clr
  Register #(.width(5)) rb (.D(Op_q[20:16]), .Q(rb_q), .clk(Clock_out));  // open: en, clr
  Register #(.width(32)) I (.D(multiplexer_2_out), .Q(I_q), .clk(Clock_out));  // open: en, clr
  Register #(.width(5)) Sa (.D(Op_q[10:6]), .Q(Sa_q), .clk(Clock_out));  // open: en, clr
  Register #(.width(5)) rd (.D(Op_q[15:11]), .Q(rd_q), .clk(Clock_out));  // open: en, clr
  Register #(.width(5)) Control (.D(Decode_c0), .Q(Control_q), .clk(Clock_out));  // open: en, clr
  Register #(.width(4)) Op_2 (.D(Decode_alu0), .Q(Op_2_q), .clk(Clock_out));  // open: en, clr
  Register #(.width(1)) WE (.D(Decode_we), .Q(WE_q), .clk(Clock_out));  // open: en, clr
  Register #(.width(32)) PC_3 (.D(PC_2_q), .Q(PC_3_q), .clk(Clock_out));  // open: en, clr
  Register #(.width(1)) S_U (.D(undriven), .Q(S_U_q), .clk(Clock_out));  // open: en, clr
  Hazard Hazard (
    .EX_MEM_we(WE_2_q), .MEM_WB_we(registerfile_1_p3), .EX_MEM_d(rd_2_q), .MEM_WB_d(registerfile_1_p4),
    .ra(ra_q), .rb(rb_q), .MEM_WB_a_hazard(Hazard_mem_wb_a_hazard[0]),
    .MEM_WB_b_hazard(Hazard_mem_wb_a_hazard[1]), .EX_MEM_a_hazard(Hazard_mem_wb_a_hazard[2]),
    .EX_MEM_b_hazard(Hazard_mem_wb_a_hazard[3]));
  Execute Execute (
    .EX_MEM(C_q), .MEM_WB(registerfile_1_p1), .Hazard(Hazard_mem_wb_a_hazard), .A(A_q), .B(B_q), .I(I_q),
    .Sa(Sa_q), .Op(Op_2_q), .Control(Control_q), .Rb(rb_q), .rd(rd_q), .WE(WE_q), .PC(PC_3_q), .S_U(S_U_q),
    .C(Execute_c), .rd_2(Execute_rd_2), .WE_2(Execute_we_2), .PC_2(Execute_pc_2));
  Register #(.width(32)) C (.D(Execute_c), .Q(C_q), .clk(Clock_out));  // open: en, clr
  Register #(.width(5)) rd_2 (.D(Execute_rd_2), .Q(rd_2_q), .clk(Clock_out));  // open: en, clr
  Register #(.width(1)) WE_2 (.D(Execute_we_2), .Q(WE_2_q), .clk(Clock_out));  // open: en, clr
  Register #(.width(32)) PC_4 (.D(Execute_pc_2), .Q(PC_4_q), .clk(Clock_out));  // open: en, clr
  Memory Memory (.C(C_q), .rd(rd_2_q), .WE(WE_2_q), .C_2(Memory_c_2), .rd_2(Memory_rd_2), .WE_2(Memory_we_2));
  Register #(.width(32)) C_2 (.D(Memory_c_2), .Q(registerfile_1_p1), .clk(Clock_out));  // open: en, clr
  Register #(.width(5)) rd_3 (.D(Memory_rd_2), .Q(registerfile_1_p4), .clk(Clock_out));  // open: en, clr
  Register #(.width(1)) WE_3 (.D(Memory_we_2), .Q(registerfile_1_p3), .clk(Clock_out));  // open: en, clr

  // Notes on the sheet:
  //   Jump/Branch Logic here later
  //   Stage: Fetch
  //   Stage: Decode
  //   Stage: Writeback
  //   Stage: Execute
  //   Stage: Memory
  //   Stage: Writeback
endmodule

module Memory (
  input  [31:0] C,
  input  [4:0] rd,
  input  WE,
  output [31:0] C_2,
  output [4:0] rd_2,
  output WE_2
);


  assign C_2 = C;
  assign rd_2 = rd;
  assign WE_2 = WE;
endmodule

module Execute (
  input  [31:0] EX_MEM,
  input  [31:0] MEM_WB,
  input  [3:0] Hazard,
  input  [31:0] A,
  input  [31:0] B,
  input  [31:0] I,
  input  [4:0] Sa,
  input  [3:0] Op,
  input  [4:0] Control,
  input  [4:0] Rb,
  input  [4:0] rd,
  input  WE,
  input  [31:0] PC,
  input  S_U,
  output [31:0] C,
  output [4:0] rd_2,
  output WE_2,
  output [31:0] PC_2
);

  wire and_1_out, and_2_out, and_3_out, comparator_1_lt, comparator_2_lt, eqz_1_c, mov_1_o,
       multiplexer_9_out, not_1_out, not_2_out, not_3_out, not_4_out, not_5_out, not_6_out, not_7_out,
       or_1_out, or_2_out, or_3_out, xor_1_out;
  wire [4:0] multiplexer_7_out;
  wire [31:0] bit_extender_1_out, mips_alu_1_p5, multiplexer_1_out, multiplexer_2_out, multiplexer_3_out,
       multiplexer_4_out, multiplexer_5_out, multiplexer_8_out, multiplexer_10_out;

  Multiplexer #(.width(32), .enable("false")) multiplexer_1 (
    .in0(A), .in1(MEM_WB), .out(multiplexer_1_out), .sel(Hazard[0]));
  Multiplexer #(.width(32), .enable("false")) multiplexer_2 (
    .in0(multiplexer_1_out), .in1(EX_MEM), .out(multiplexer_2_out), .sel(Hazard[2]));
  Multiplexer #(.width(32), .enable("false")) multiplexer_3 (
    .in0(B), .in1(MEM_WB), .out(multiplexer_3_out), .sel(Hazard[1]));
  Multiplexer #(.width(32), .enable("false")) multiplexer_4 (
    .in0(multiplexer_3_out), .in1(EX_MEM), .out(multiplexer_4_out), .sel(Hazard[3]));
  Multiplexer #(.width(32), .enable("false")) multiplexer_5 (
    .in0(multiplexer_4_out), .in1(I), .out(multiplexer_5_out), .sel(Control[4]));
  Multiplexer #(.width(5), .enable("false")) multiplexer_6 (.in0(Rb), .in1(rd), .out(rd_2), .sel(not_1_out));
  not not_1 (not_1_out, Control[4]);
  Multiplexer #(.width(5), .enable("false")) multiplexer_7 (
    .in0(multiplexer_2_out[4:0]), .in1(Sa), .out(multiplexer_7_out), .sel(Control[2]));
  // Mips_ALU mips_alu_1: pin names not known; wires that end beside it: multiplexer_2_out, multiplexer_5_out, Op, multiplexer_7_out, mips_alu_1_p5
  EQZ eqz_1 (.A(multiplexer_5_out), .C(eqz_1_c));
  Comparator #(.width(32)) comparator_1 (
    .a(multiplexer_2_out), .b(multiplexer_5_out), .lt(comparator_1_lt));  // open: gt, eq
  Comparator #(.width(32), .mode("unsigned")) comparator_2 (
    .a(multiplexer_2_out), .b(multiplexer_5_out), .lt(comparator_2_lt));  // open: gt, eq
  Multiplexer #(.width(32), .enable("false")) multiplexer_8 (
    .in0(multiplexer_2_out), .in1(mips_alu_1_p5), .out(multiplexer_8_out), .sel(and_1_out));
  and and_1 (and_1_out, not_2_out, not_3_out);
  not not_2 (not_2_out, mov_1_o);
  MOV mov_1 (.Op(Control), .O(mov_1_o));
  not not_3 (not_3_out, Control[0]);
  Multiplexer #(.enable("false")) multiplexer_9 (
    .in0(comparator_1_lt), .in1(comparator_2_lt), .out(multiplexer_9_out), .sel(Control[2]));
  assign bit_extender_1_out = {{31{1'b0}}, multiplexer_9_out};  // Bit_Extender bit_extender_1
  xor xor_1 (xor_1_out, eqz_1_c, Control[0]);
  not not_4 (not_4_out, Control[1]);
  Multiplexer #(.width(32), .enable("false")) multiplexer_10 (
    .in0(multiplexer_8_out), .in1(multiplexer_5_out), .out(multiplexer_10_out), .sel(or_1_out));
  or or_1 (or_1_out, and_2_out, and_3_out);
  and and_2 (and_2_out, and_1_out, Control[1]);
  and and_3 (and_3_out, Control[0], not_6_out, Control[2], not_5_out, Control[4]);
  not not_5 (not_5_out, Control[3]);
  not not_6 (not_6_out, Control[1]);
  or or_2 (or_2_out, rd_2[0], rd_2[1], rd_2[2], rd_2[3], rd_2[4]);
  or or_3 (or_3_out, xor_1_out, not_4_out);
  Multiplexer #(.width(32), .enable("false")) multiplexer_11 (
    .in0(bit_extender_1_out), .in1(multiplexer_10_out), .out(C), .sel(not_7_out));
  not not_7 (not_7_out, Control[3]);
  and and_4 (WE_2, WE, or_2_out, or_3_out);

  assign PC_2 = PC;
endmodule

module Decode (
  input  f5,
  input  f4,
  input  f3,
  input  f2,
  input  f1,
  input  f0,
  input  op5,
  input  op4,
  input  op3,
  input  op2,
  input  op1,
  input  op0,
  output LUI,
  output c4,
  output c3,
  output c2,
  output c1,
  output c0,
  output alu3,
  output alu2,
  output alu1,
  output alu0,
  output WE
);

  wire and_3_out, and_4_out, and_5_out, and_6_out, and_7_out, and_8_out, and_10_out, and_11_out, and_12_out,
       and_13_out, and_14_out, and_15_out, and_16_out, and_17_out, and_18_out, and_20_out, and_21_out,
       and_22_out, and_23_out, and_24_out, and_25_out, nand_1_out, nand_2_out, nand_3_out, nand_4_out,
       nand_5_out, nand_6_out, nor_1_out, nor_2_out, not_1_out, not_2_out, not_3_out, not_4_out, not_5_out,
       not_6_out, not_7_out, not_8_out, not_9_out, not_10_out, not_11_out, not_12_out, not_13_out,
       not_14_out, not_15_out, not_16_out, not_17_out, not_18_out, not_19_out, not_20_out, not_21_out,
       not_22_out, not_23_out, not_24_out, not_25_out, not_26_out, not_27_out, not_28_out, not_29_out,
       not_30_out, not_31_out, not_32_out, not_33_out, not_34_out, not_35_out, not_36_out, not_37_out,
       not_38_out, not_39_out, not_40_out, not_41_out, not_42_out, not_43_out, not_44_out, not_45_out,
       not_46_out, not_47_out, not_48_out, not_49_out, not_50_out, not_51_out, not_52_out, not_53_out,
       not_54_out, not_55_out, not_56_out, not_57_out, not_58_out, not_59_out, not_60_out, or_1_out,
       or_2_out, or_6_out;

  and and_1 (LUI, op2, op1, op0);
  not not_1 (not_1_out, op5);
  and and_2 (c4, not_1_out, not_2_out, op3);
  not not_2 (not_2_out, op4);
  not not_3 (not_3_out, f4);
  not not_4 (not_4_out, f2);
  nand nand_1 (nand_1_out, op5, op4, op3, op2, op1, op0);
  not not_5 (not_5_out, op5);
  not not_6 (not_6_out, op4);
  not not_7 (not_7_out, op2);
  not not_8 (not_8_out, f0);
  and and_3 (and_3_out, not_8_out, not_9_out);
  not not_9 (not_9_out, f2);
  not not_10 (not_10_out, f2);
  and and_4 (and_4_out, not_10_out, not_11_out);
  not not_11 (not_11_out, f3);
  not not_12 (not_12_out, f5);
  not not_13 (not_13_out, f4);
  not not_14 (not_14_out, f2);
  nand nand_2 (nand_2_out, op0, op1, op2, op3, op4, op5);
  not not_15 (not_15_out, f5);
  not not_16 (not_16_out, f4);
  not not_17 (not_17_out, f2);
  nand nand_3 (nand_3_out, op0, op1, op2, op3, op4, op5);
  not not_18 (not_18_out, op5);
  not not_19 (not_19_out, op4);
  not not_20 (not_20_out, op5);
  not not_21 (not_21_out, op4);
  not not_22 (not_22_out, f4);
  not not_23 (not_23_out, f3);
  not not_24 (not_24_out, op5);
  not not_25 (not_25_out, op4);
  not not_26 (not_26_out, op3);
  not not_27 (not_27_out, op2);
  not not_28 (not_28_out, op1);
  not not_29 (not_29_out, op0);
  not not_30 (not_30_out, f5);
  not not_31 (not_31_out, f4);
  not not_32 (not_32_out, f3);
  not not_33 (not_33_out, f4);
  not not_34 (not_34_out, f3);
  not not_35 (not_35_out, f4);
  not not_36 (not_36_out, f3);
  not not_37 (not_37_out, f2);
  not not_38 (not_38_out, op5);
  not not_39 (not_39_out, op4);
  not not_40 (not_40_out, op1);
  not not_41 (not_41_out, f4);
  not not_42 (not_42_out, f3);
  nand nand_4 (nand_4_out, op0, op1, op2, op3, op4, op5);
  not not_43 (not_43_out, f5);
  not not_44 (not_44_out, f4);
  not not_45 (not_45_out, f3);
  nand nand_5 (nand_5_out, op0, op1, op2, op3, op4, op5);
  not not_46 (not_46_out, f0);
  and and_5 (and_5_out, not_46_out, not_47_out);
  not not_47 (not_47_out, f2);
  not not_48 (not_48_out, f2);
  and and_6 (and_6_out, not_48_out, not_49_out);
  not not_49 (not_49_out, f3);
  and and_7 (and_7_out, f5, not_3_out, f3, not_4_out, f1, nand_1_out);
  and and_8 (and_8_out, not_5_out, not_6_out, op3, not_7_out, op1);
  not not_50 (not_50_out, op5);
  not not_51 (not_51_out, op4);
  not not_52 (not_52_out, op2);
  not not_53 (not_53_out, op0);
  or or_1 (or_1_out, and_3_out, and_4_out);
  and and_9 (c1, not_12_out, not_13_out, f3, not_14_out, f1, nand_2_out);
  and and_10 (and_10_out, not_15_out, not_16_out, f3, not_17_out, f1, f0, nand_3_out);
  and and_11 (and_11_out, not_18_out, not_19_out, op3, op2, op1, op0);
  and and_12 (and_12_out, not_20_out, not_21_out, op3, op2);
  and and_13 (and_13_out, f5, not_22_out, not_23_out, f2, not_24_out, not_25_out, not_26_out, not_27_out, not_28_out, not_29_out);
  not not_54 (not_54_out, op5);
  not not_55 (not_55_out, op4);
  not not_56 (not_56_out, op0);
  and and_14 (and_14_out, not_30_out, not_31_out, not_32_out, f1);
  and and_15 (and_15_out, f5, not_33_out, not_34_out, f2, f1);
  and and_16 (and_16_out, f5, not_35_out, not_36_out, not_37_out, f1, f0);
  and and_17 (and_17_out, not_38_out, not_39_out, op3, not_40_out, op0);
  and and_18 (and_18_out, f5, not_41_out, not_42_out, f0, nand_4_out);
  and and_19 (alu0, not_43_out, not_44_out, not_45_out, f1, f0, nand_5_out);
  not not_57 (not_57_out, op5);
  not not_58 (not_58_out, op4);
  not not_59 (not_59_out, op2);
  not not_60 (not_60_out, op0);
  nor nor_1 (nor_1_out, op0, op1, op2, op3, op4, op5);
  or or_2 (or_2_out, and_5_out, and_6_out);
  or or_3 (c3, and_7_out, and_8_out);
  and and_20 (and_20_out, not_50_out, not_51_out, op3, not_52_out, op1, not_53_out);
  nor nor_2 (nor_2_out, op0, op1, op2, op3, op4, op5);
  and and_21 (and_21_out, nor_2_out, or_1_out);
  or or_4 (c0, and_10_out, and_11_out);
  or or_5 (alu3, and_12_out, and_13_out);
  and and_22 (and_22_out, not_54_out, not_55_out, op3, op2, op1, not_56_out);
  nand nand_6 (nand_6_out, op0, op1, op2, op3, op4, op5);
  and and_23 (and_23_out, nand_6_out, or_6_out);
  or or_6 (or_6_out, and_14_out, and_15_out, and_16_out);
  or or_7 (alu1, and_17_out, and_18_out);
  and and_24 (and_24_out, not_57_out, not_58_out, op3, not_59_out, op1, not_60_out);
  and and_25 (and_25_out, nor_1_out, or_2_out);
  or or_8 (c2, and_20_out, and_21_out);
  or or_9 (alu2, and_22_out, and_23_out);
  or or_10 (WE, and_24_out, and_25_out);
endmodule

module EQZ (
  input  [31:0] A,
  output C
);

  nor nor_1 (C, A[0], A[1], A[2], A[3], A[4], A[5], A[6], A[7], A[8], A[9], A[10], A[11], A[12], A[13], A[14], A[15], A[16], A[17], A[18], A[19], A[20], A[21], A[22], A[23], A[24], A[25], A[26], A[27], A[28], A[29], A[30], A[31]);

  // Notes on the sheet:
  //   This circuit tests A == 0
endmodule

module Hazard (
  input  EX_MEM_we,
  input  MEM_WB_we,
  input  [4:0] EX_MEM_d,
  input  [4:0] MEM_WB_d,
  input  [4:0] ra,
  input  [4:0] rb,
  output MEM_WB_a_hazard,
  output MEM_WB_b_hazard,
  output EX_MEM_a_hazard,
  output EX_MEM_b_hazard
);

  wire eq5_1_out, eq5_2_out, eq5_3_out, eq5_4_out;

  Eq5 eq5_1 (.A(MEM_WB_d), .B(ra), .Out(eq5_1_out));
  Eq5 eq5_2 (.A(MEM_WB_d), .B(rb), .Out(eq5_2_out));
  and and_1 (MEM_WB_a_hazard, MEM_WB_we, eq5_1_out);
  and and_2 (MEM_WB_b_hazard, MEM_WB_we, eq5_2_out);
  Eq5 eq5_3 (.A(EX_MEM_d), .B(ra), .Out(eq5_3_out));
  Eq5 eq5_4 (.A(EX_MEM_d), .B(rb), .Out(eq5_4_out));
  and and_3 (EX_MEM_a_hazard, EX_MEM_we, eq5_3_out);
  and and_4 (EX_MEM_b_hazard, EX_MEM_we, eq5_4_out);
endmodule

module Eq5 (
  input  [4:0] A,
  input  [4:0] B,
  output Out
);

  wire [4:0] xor_1_out;

  assign xor_1_out = A ^ B;  // XOR_Gate xor_1, 5 bits wide
  nor nor_1 (Out, xor_1_out[0], xor_1_out[1], xor_1_out[2], xor_1_out[3], xor_1_out[4]);
endmodule

// +4
module add4 (
  input  [31:0] A,
  output [31:0] C
);

  wire and_1_out, and_2_out, and_3_out, and_4_out, and_5_out, and_6_out, and_7_out, and_8_out, and_9_out,
       and_10_out, and_11_out, and_12_out, and_13_out, and_14_out, and_15_out, and_16_out, and_17_out,
       and_18_out, and_19_out, and_20_out, and_21_out, and_22_out, and_23_out, and_24_out, and_25_out,
       and_26_out, and_27_out, and_28_out;

  and and_1 (and_1_out, A[2], A[3]);
  and and_2 (and_2_out, A[2], A[3], A[4]);
  and and_3 (and_3_out, A[2], A[3], A[4], A[5]);
  and and_4 (and_4_out, A[2], A[3], A[4], A[5], A[6]);
  and and_5 (and_5_out, A[2], A[3], A[4], A[5], A[6], A[7]);
  and and_6 (and_6_out, A[2], A[3], A[4], A[5], A[6], A[7], A[8]);
  and and_7 (and_7_out, A[2], A[3], A[4], A[5], A[6], A[7], A[8], A[9]);
  and and_8 (and_8_out, A[2], A[3], A[4], A[5], A[6], A[7], A[8], A[9], A[10]);
  and and_9 (and_9_out, A[2], A[3], A[4], A[5], A[6], A[7], A[8], A[9], A[10], A[11]);
  and and_10 (and_10_out, A[2], A[3], A[4], A[5], A[6], A[7], A[8], A[9], A[10], A[11], A[12]);
  and and_11 (and_11_out, A[2], A[3], A[4], A[5], A[6], A[7], A[8], A[9], A[10], A[11], A[12], A[13]);
  and and_12 (and_12_out, A[2], A[3], A[4], A[5], A[6], A[7], A[8], A[9], A[10], A[11], A[12], A[13], A[14]);
  and and_13 (and_13_out, A[2], A[3], A[4], A[5], A[6], A[7], A[8], A[9], A[10], A[11], A[12], A[13], A[14], A[15]);
  and and_14 (and_14_out, A[2], A[3], A[4], A[5], A[6], A[7], A[8], A[9], A[10], A[11], A[12], A[13], A[14], A[15], A[16]);
  and and_15 (and_15_out, A[2], A[3], A[4], A[5], A[6], A[7], A[8], A[9], A[10], A[11], A[12], A[13], A[14], A[15], A[16], A[17]);
  and and_16 (and_16_out, A[2], A[3], A[4], A[5], A[6], A[7], A[8], A[9], A[10], A[11], A[12], A[13], A[14], A[15], A[16], A[17], A[18]);
  and and_17 (and_17_out, A[2], A[3], A[4], A[5], A[6], A[7], A[8], A[9], A[10], A[11], A[12], A[13], A[14], A[15], A[16], A[17], A[18], A[19]);
  and and_18 (and_18_out, A[2], A[3], A[4], A[5], A[6], A[7], A[8], A[9], A[10], A[11], A[12], A[13], A[14], A[15], A[16], A[17], A[18], A[19], A[20]);
  and and_19 (and_19_out, A[2], A[3], A[4], A[5], A[6], A[7], A[8], A[9], A[10], A[11], A[12], A[13], A[14], A[15], A[16], A[17], A[18], A[19], A[20], A[21]);
  and and_20 (and_20_out, A[2], A[3], A[4], A[5], A[6], A[7], A[8], A[9], A[10], A[11], A[12], A[13], A[14], A[15], A[16], A[17], A[18], A[19], A[20], A[21], A[22]);
  and and_21 (and_21_out, A[2], A[3], A[4], A[5], A[6], A[7], A[8], A[9], A[10], A[11], A[12], A[13], A[14], A[15], A[16], A[17], A[18], A[19], A[20], A[21], A[22], A[23]);
  and and_22 (and_22_out, A[2], A[3], A[4], A[5], A[6], A[7], A[8], A[9], A[10], A[11], A[12], A[13], A[14], A[15], A[16], A[17], A[18], A[19], A[20], A[21], A[22], A[23], A[24]);
  and and_23 (and_23_out, A[2], A[3], A[4], A[5], A[6], A[7], A[8], A[9], A[10], A[11], A[12], A[13], A[14], A[15], A[16], A[17], A[18], A[19], A[20], A[21], A[22], A[23], A[24], A[25]);
  and and_24 (and_24_out, A[2], A[3], A[4], A[5], A[6], A[7], A[8], A[9], A[10], A[11], A[12], A[13], A[14], A[15], A[16], A[17], A[18], A[19], A[20], A[21], A[22], A[23], A[24], A[25], A[26]);
  and and_25 (and_25_out, A[2], A[3], A[4], A[5], A[6], A[7], A[8], A[9], A[10], A[11], A[12], A[13], A[14], A[15], A[16], A[17], A[18], A[19], A[20], A[21], A[22], A[23], A[24], A[25], A[26], A[27]);
  and and_26 (and_26_out, A[2], A[3], A[4], A[5], A[6], A[7], A[8], A[9], A[10], A[11], A[12], A[13], A[14], A[15], A[16], A[17], A[18], A[19], A[20], A[21], A[22], A[23], A[24], A[25], A[26], A[27], A[28]);
  and and_27 (and_27_out, A[2], A[3], A[4], A[5], A[6], A[7], A[8], A[9], A[10], A[11], A[12], A[13], A[14], A[15], A[16], A[17], A[18], A[19], A[20], A[21], A[22], A[23], A[24], A[25], A[26], A[27], A[28], A[29]);
  and and_28 (and_28_out, A[2], A[3], A[4], A[5], A[6], A[7], A[8], A[9], A[10], A[11], A[12], A[13], A[14], A[15], A[16], A[17], A[18], A[19], A[20], A[21], A[22], A[23], A[24], A[25], A[26], A[27], A[28], A[29], A[30]);
  xor xor_1 (C[3], A[2], A[3]);
  xor xor_2 (C[4], and_1_out, A[4]);
  xor xor_3 (C[5], and_2_out, A[5]);
  xor xor_4 (C[6], and_3_out, A[6]);
  xor xor_5 (C[7], and_4_out, A[7]);
  xor xor_6 (C[8], and_5_out, A[8]);
  xor xor_7 (C[9], and_6_out, A[9]);
  xor xor_8 (C[10], and_7_out, A[10]);
  xor xor_9 (C[11], and_8_out, A[11]);
  xor xor_10 (C[12], and_9_out, A[12]);
  xor xor_11 (C[13], and_10_out, A[13]);
  xor xor_12 (C[14], and_11_out, A[14]);
  xor xor_13 (C[15], and_12_out, A[15]);
  xor xor_14 (C[16], and_13_out, A[16]);
  xor xor_15 (C[17], and_14_out, A[17]);
  xor xor_16 (C[18], and_15_out, A[18]);
  xor xor_17 (C[19], and_16_out, A[19]);
  xor xor_18 (C[20], and_17_out, A[20]);
  xor xor_19 (C[21], and_18_out, A[21]);
  xor xor_20 (C[22], and_19_out, A[22]);
  xor xor_21 (C[23], and_20_out, A[23]);
  xor xor_22 (C[24], and_21_out, A[24]);
  xor xor_23 (C[25], and_22_out, A[25]);
  xor xor_24 (C[26], and_23_out, A[26]);
  xor xor_25 (C[27], and_24_out, A[27]);
  xor xor_26 (C[28], and_25_out, A[28]);
  xor xor_27 (C[29], and_26_out, A[29]);
  xor xor_28 (C[30], and_27_out, A[30]);
  xor xor_29 (C[31], and_28_out, A[31]);
  not not_1 (C[2], A[2]);

  assign C[1:0] = A[1:0];
endmodule

module MOV (
  input  [4:0] Op,
  output O
);

  wire and_1_out, and_2_out, not_1_out, not_2_out, not_3_out, not_4_out;

  not not_1 (not_1_out, Op[2]);
  not not_2 (not_2_out, Op[0]);
  not not_3 (not_3_out, Op[3]);
  not not_4 (not_4_out, Op[4]);
  and and_1 (and_1_out, Op[0], Op[1], not_1_out, not_3_out, not_4_out);
  and and_2 (and_2_out, not_2_out, Op[1], Op[2], not_3_out, not_4_out);
  or or_1 (O, and_1_out, and_2_out);
endmodule
